# Fritzing sketch circuit-schematic (saved by Fritzing 0.9.3b)
breadboards: 1

parts:
  Part1 = Arduino Mega 2560 (Rev3)
  S1 = H-Bridge with L298N
  M1 = Stepper Motor - Bipolar
  Raspberry_Pi_1 = Raspberry Pi 3 [part_number=RPI-3-V1.2]  # not connected
  VCC1 = Battery block 9V
  M2 = DC Motor  # not connected

nets:
  N1: Part1.D11_PWM, S1.IN4
  N2: Part1.D10_PWM, S1.IN3
  N3: Part1.D9_PWM, S1.IN2
  N4: Part1.D8_PWM, S1.IN1
  5V: Part1.5V, S1.5V
  N5: Part1.GND, VCC1.-
  N6: Part1.D5_PWM, S1.ENA
  N7: Part1.D6_PWM, S1.ENB
  N8: S1.12V, VCC1.+
  N9: S1.M1-01, M1.A
  N10: S1.M1-02, M1.C
  N11: S1.M2-01, M1.D
  N12: S1.M2-02, M1.B

notes:
  First two wires, green & black for one winding
  Seond pair of wiring for second winding
  OUT1 and OUT2
  OUT3 & OUT4
  PIN 8-11
  PINS TO IN1,IN2,IN3,IN4

custom parts:
  H-Bridge with L298N: h-bridge

// code stored in the sketch: test_pump.ino
// Define Arduino pins for L298N control const int IN1 = 8; // Port A, coil 1 (A+) const int IN2 = 9; // Port A, coil 1 (A-) const int IN3 = 10; // Port B, coil 2 (B+) const int IN4 = 11; // Port B, coil 2 (B-) const int ENA = 5; // Enable A (PWM for speed control of Port A) const int ENB = 6; // Enable B (PWM for speed control of Port B)
// Step sequence for CW rotation (from KPHM100 manual) int stepSequenceCW[4][4] = { {HIGH, HIGH, LOW, LOW}, // Step 1: A+ and A- energized {LOW, HIGH, HIGH, LOW}, // Step 2: A- and B+ energized {LOW, LOW, HIGH, HIGH}, // Step 3: B+ and B- energized {HIGH, LOW, LOW, HIGH} // Step 4: A+ and B- energized };
// Step sequence for CCW rotation (reverse of CW) int stepSequenceCCW[4][4] = { {HIGH, LOW, LOW, HIGH}, // Step 4 reversed {LOW, LOW, HIGH, HIGH}, // Step 3 reversed {LOW, HIGH, HIGH, LOW}, // Step 2 reversed {HIGH, HIGH, LOW, LOW} // Step 1 reversed };
int currentStep = 0; // Current step in the sequence int direction = 1; // 1 for CW, -1 for CCW int motorSpeed = 100; // Initial speed (PWM value 0-255, adjust as needed)
void setup() { // Initialize serial communication for debugging Serial.begin(9600);
// Set all pins as outputs pinMode(IN1, OUTPUT); pinMode(IN2, OUTPUT); pinMode(IN3, OUTPUT); pinMode(IN4, OUTPUT); pinMode(ENA, OUTPUT); pinMode(ENB, OUTPUT);
// Initialize pins to LOW digitalWrite(IN1, LOW); digitalWrite(IN2, LOW); digitalWrite(IN3, LOW); digitalWrite(IN4, LOW); analogWrite(ENA, motorSpeed); // Set initial speed for Port A analogWrite(ENB, motorSpeed); // Set initial speed for Port B }
void loop() { // Run the motor at the current step if (direction == 1) { // CW rotation digitalWrite(IN1, stepSequenceCW[currentStep][0]); digitalWrite(IN2, stepSequenceCW[currentStep][1]); digitalWrite(IN3, stepSequenceCW[currentStep][2]); digitalWrite(IN4, stepSequenceCW[currentStep][3]); } else { // CCW rotation digitalWrite(IN1, stepSequenceCCW[currentStep][0]); digitalWrite(IN2, stepSequenceCCW[currentStep][1]); digitalWrite(IN3, stepSequenceCCW[currentStep][2]); digitalWrite(IN4, stepSequenceCCW[currentStep][3]); }
// Delay to control speed (adjust for desired RPM) delay(5); // Adjust this delay to change motor speed (smaller = faster)
// Move to the next step currentStep = (currentStep + 1) % 4;
// Example: Change direction and speed via serial input (for testing) if (Serial.available() > 0) { char command = Serial.read(); switch (command) { case 'f': // Forward (CW) direction = 1; Serial.println("Moving Forward (CW)"); break; case 'b': // Backward (CCW) direction = -1; Serial.println("Moving Backward (CCW)"); break; case 's': // Stop digitalWrite(IN1, LOW); digitalWrite(IN2, LOW); digitalWrite(IN3, LOW); digitalWrite(IN4, LOW); Serial.println("Stopped"); break; case '+': // Increase speed motorSpeed += 50; if (motorSpeed > 255) motorSpeed = 255; // Limit PWM to 255 analogWrite(ENA, motorSpeed); analogWrite(ENB, motorSpeed); Serial.print("Speed increased to "); Serial.println(motorSpeed); break; case '-': // Decrease speed motorSpeed -= 50; if (motorSpeed < 0) motorSpeed = 0; analogWrite(ENA, motorSpeed); analogWrite(ENB, motorSpeed); Serial.print("Speed decreased to "); Serial.println(motorSpeed); break; } } }
